// Logisim project Eduardo Cardoso - Atividade.circ as structural Verilog: 1 circuit, main circuit main
module main (
  input  _1,
  input  in_2,
  input  _3,
  output out_4
);

  wire and_1_out, and_2_out, not_1_out;

  not not_1 (not_1_out, _3);
  and and_1 (and_1_out, in_2, not_1_out);
  and and_2 (and_2_out, _1, not_1_out);
  or or_1 (out_4, and_2_out, and_1_out);

  // Notes on the sheet:
  //   2
endmodule
